// Logisim project parte1_cache.circ as structural Verilog: 5 circuits, main circuit Cache
module XOR_manual (
  input  A,
  input  B,
  output S
);

  wire and_1_out, and_2_out, not_1_out, not_2_out;

  and and_1 (and_1_out, A, not_1_out);
  not not_1 (not_1_out, B);
  not not_2 (not_2_out, A);
  and and_2 (and_2_out, not_2_out, B);
  or or_1 (S, and_1_out, and_2_out);
endmodule

module Cache (
  input  [7:0] Endereco_Atual,
  input  Usar_Seguinte,
  input  Reset,
  input  [7:0] Dado_Escrita,
  output Iguais,
  output ACERTO,
  output T0,
  output T1,
  output T2,
  output A2,
  output A1,
  output A0
);

  wire clock_1_out, detectorprimo_1_primo, not_1_out, or_1_out, reg_cache_1_valido_indice, XOR_T0_s,
       XOR_T1_s, XOR_T2_s;
  wire [2:0] reg_cache_1_rotulo_guardado;
  wire [7:0] counter_1_q, somador_manual_1_endereco_seguinte;
  wire [7:6] multiplexer_1_out;

  Multiplexer #(.width(8)) multiplexer_1 (
    .in0(Endereco_Atual), .in1(somador_manual_1_endereco_seguinte),
    .out({multiplexer_1_out, T2, T1, T0, A2, A1, A0}), .sel(Usar_Seguinte));
  Somador_Manual somador_manual_1 (
    .Endereco_Atual(Endereco_Atual), .Endereco_Seguinte(somador_manual_1_endereco_seguinte));
  LED led_1 (.in(detectorprimo_1_primo));
  DetectorPrimo detectorprimo_1 (.V0(T0), .V1(T1), .V2(T2), .V3(1'b0), .Primo(detectorprimo_1_primo));
  Clock clock_1 (.out(clock_1_out));
  not not_1 (not_1_out, clock_1_out);
  RAM #(.addrWidth(3)) ram_1 (
    .addr({A2, A1, A0}), .we(ACERTO), .oe(1'b1), .clk(not_1_out), .din(Dado_Escrita));  // open: dout
  XOR_manual XOR_T0 (.A(T0), .B(reg_cache_1_rotulo_guardado[0]), .S(XOR_T0_s));
  XOR_manual XOR_T1 (.A(T1), .B(reg_cache_1_rotulo_guardado[1]), .S(XOR_T1_s));
  XOR_manual XOR_T2 (.A(T2), .B(reg_cache_1_rotulo_guardado[2]), .S(XOR_T2_s));
  Reg_Cache reg_cache_1 (
    .ACERTO(ACERTO), .A2(A2), .A1(A1), .Clock(clock_1_out), .Reg_Rotulo({T2, T1, T0}), .Reset(Reset),
    .Rotulo_Guardado(reg_cache_1_rotulo_guardado), .Valido_Indice(reg_cache_1_valido_indice));
  not not_2 (Iguais, or_1_out);
  or or_1 (or_1_out, XOR_T0_s, XOR_T1_s, XOR_T2_s);
  and and_1 (ACERTO, Iguais, reg_cache_1_valido_indice);
  Counter counter_1 (.clr(Reset), .count(ACERTO), .clk(clock_1_out), .Q(counter_1_q));  // open: load, up, D, carry
  // BCD_to_7_Segment_decoder bcd_to_7_segment_decoder_1: pin names not known; wires that end beside it: counter_1_q[3:0]
  _7_Segment_Display #(.decimalPoint("false")) u_7_segment_display_1 ();  // open: g, f, a, b, e, d, c
endmodule

module Reg_Cache (
  input  ACERTO,
  input  A2,
  input  A1,
  input  Clock,
  input  [2:0] Reg_Rotulo,
  input  Reset,
  output [2:0] Rotulo_Guardado,
  output Valido_Indice
);

  wire d_ff_1_q, d_ff_2_q, d_ff_3_q, d_ff_4_q, decoder_1_out0, decoder_1_out1, decoder_1_out2,
       decoder_1_out3, not_1_out, or_1_out, or_2_out, or_3_out, or_4_out;
  wire [2:0] Reg_Rotulo_0_q, Reg_Rotulo_1_q, Reg_Rotulo_2_q, Reg_Rotulo_3_q;

  not not_1 (not_1_out, ACERTO);
  Decoder #(.select(2)) decoder_1 (
    .out0(decoder_1_out0), .out1(decoder_1_out1), .out2(decoder_1_out2), .out3(decoder_1_out3),
    .sel({A1, A2}), .en(not_1_out));
  Register #(.width(3)) Reg_Rotulo_0 (
    .D(Reg_Rotulo), .en(decoder_1_out0), .clk(Clock), .Q(Reg_Rotulo_0_q));  // open: clr
  or or_1 (or_1_out, d_ff_1_q, decoder_1_out0);
  Register #(.width(3)) Reg_Rotulo_1 (
    .D(Reg_Rotulo), .en(decoder_1_out1), .clk(Clock), .Q(Reg_Rotulo_1_q));  // open: clr
  or or_2 (or_2_out, d_ff_2_q, decoder_1_out1);
  Register #(.width(3)) Reg_Rotulo_2 (
    .D(Reg_Rotulo), .en(decoder_1_out2), .clk(Clock), .Q(Reg_Rotulo_2_q));  // open: clr
  or or_3 (or_3_out, d_ff_3_q, decoder_1_out2);
  Register #(.width(3)) Reg_Rotulo_3 (
    .D(Reg_Rotulo), .en(decoder_1_out3), .clk(Clock), .Q(Reg_Rotulo_3_q));  // open: clr
  or or_4 (or_4_out, d_ff_4_q, decoder_1_out3);
  D_Flip_Flop d_ff_1 (.D(or_1_out), .clk(Clock), .Q(d_ff_1_q), .reset(Reset));  // open: Qn, preset
  D_Flip_Flop d_ff_2 (.D(or_2_out), .clk(Clock), .Q(d_ff_2_q), .reset(Reset));  // open: Qn, preset
  D_Flip_Flop d_ff_3 (.D(or_3_out), .clk(Clock), .Q(d_ff_3_q), .reset(Reset));  // open: Qn, preset
  D_Flip_Flop d_ff_4 (.D(or_4_out), .clk(Clock), .Q(d_ff_4_q), .reset(Reset));  // open: Qn, preset
  Multiplexer #(.select(2), .width(3)) multiplexer_1 (
    .in0(Reg_Rotulo_0_q), .in1(Reg_Rotulo_1_q), .in2(Reg_Rotulo_2_q), .in3(Reg_Rotulo_3_q),
    .out(Rotulo_Guardado), .sel({A1, A2}));
  Multiplexer #(.select(2)) multiplexer_2 (
    .in0(d_ff_1_q), .in1(d_ff_2_q), .in2(d_ff_3_q), .in3(d_ff_4_q), .out(Valido_Indice), .sel({A1, A2}));
endmodule

module Somador_Manual (
  input  [7:0] Endereco_Atual,
  output [7:0] Endereco_Seguinte
);

  Adder adder_1 (.a(Endereco_Atual), .b({8{1'b0}}), .out(Endereco_Seguinte), .cin(1'b1));  // open: cout
endmodule

module DetectorPrimo (
  input  V0,
  input  V1,
  input  V2,
  input  V3,
  output Primo
);

  wire and_1_out, and_2_out, and_3_out, and_4_out, not_1_out, not_2_out, not_3_out;

  not not_1 (not_1_out, V1);
  not not_2 (not_2_out, V2);
  not not_3 (not_3_out, V3);
  and and_1 (and_1_out, not_3_out, not_2_out, V1);
  and and_2 (and_2_out, not_3_out, V1, V0);
  and and_3 (and_3_out, V2, not_1_out, V0);
  and and_4 (and_4_out, not_2_out, V1, V0);
  or or_1 (Primo, and_1_out, and_2_out, and_3_out, and_4_out);
endmodule
