// Logisim project parte1_memoria.circ as structural Verilog
module MemoriaPrincipal (
  input  A0,
  input  A1,
  input  A2,
  input  A3,
  input  A4,
  input  A5,
  input  WE,
  input  Pino_R,
  input  [7:0] Dados_In,
  input  Constante,
  input  [7:0] Entrada_Externa,
  output CS_ROM,
  output CS_RAM,
  output CS_REG,
  output CS_IO,
  output [7:0] Dados_Out
);

  wire and_5_out, and_6_out, and_7_out, clock_1_out, geradorparidade_1_p, geradorparidade_2_p, not_1_out,
       not_2_out, not_3_out, RAM_Comp_Pr_dout, xor_1_out;
  wire [3:0] CS_IO_R_q, CS_IO_R_q_2;
  wire [7:0] bancoreg_1_dados_out, multiplexer_1_out, RAM_P_dout, rom_1_data;

  Clock #(.phaseOffset(1)) clock_1 (.out(clock_1_out));
  not not_1 (not_1_out, A5);
  not not_2 (not_2_out, A4);
  and and_1 (CS_ROM, not_2_out, not_1_out);
  and and_2 (CS_RAM, not_1_out, A4);
  and and_3 (CS_REG, not_2_out, A5);
  and and_4 (CS_IO, A4, A5);
  and and_5 (and_5_out, WE, CS_REG);
  and and_6 (and_6_out, CS_IO, A0, WE);
  GeradorParidade geradorparidade_1 (.Dado(Dados_In), .P(geradorparidade_1_p));
  not not_3 (not_3_out, geradorparidade_1_p);
  and and_7 (and_7_out, WE, CS_RAM);
  Register CS_IO_R (.D(Dados_In), .en(and_6_out), .clk(Pino_R), .Q({CS_IO_R_q_2, CS_IO_R_q}));  // open: clr
  RAM #(.addrWidth(4)) RAM_P (
    .addr({A3, A2, A1, A0}), .we(and_7_out), .oe(CS_RAM), .clk(clock_1_out), .din(Dados_In), .dout(RAM_P_dout));
  ROM #(.addrWidth(4)) rom_1 (.addr({A3, A2, A1, A0}), .data(rom_1_data));
  RAM #(.addrWidth(4), .dataWidth(1)) RAM_Comp_Pr (
    .addr({A3, A2, A1, A0}), .we(and_7_out), .oe(CS_RAM), .clk(clock_1_out), .din(not_3_out),
    .dout(RAM_Comp_Pr_dout));
  Hex_Digit_Display hex_digit_display_1 (.value(CS_IO_R_q_2));  // open: dp
  BancoReg bancoreg_1 (
    .Endereco({A3, A2, A1, A0}), .Dados_In(Dados_In), .Clock(clock_1_out), .WE(and_5_out), .Pino_R(Pino_R),
    .Dados_Out(bancoreg_1_dados_out));
  Multiplexer #(.width(8)) multiplexer_1 (
    .in0(Entrada_Externa), .in1({CS_IO_R_q_2, CS_IO_R_q}), .out(multiplexer_1_out), .sel(A0));
  GeradorParidade geradorparidade_2 (.Dado(RAM_P_dout), .P(geradorparidade_2_p));
  Multiplexer #(.select(2), .width(8)) multiplexer_2 (
    .in0(RAM_P_dout), .in1(rom_1_data), .in2(bancoreg_1_dados_out), .in3(multiplexer_1_out), .out(Dados_Out),
    .sel({A5, A4}));
  xor xor_1 (xor_1_out, geradorparidade_2_p, RAM_Comp_Pr_dout);
  // Probe on xor_1_out
  LED Paridade_OK (.in(xor_1_out));
endmodule

module GeradorParidade (
  input  [7:0] Dado,
  output P
);

  xor xor_1 (P, Dado[0], Dado[1], Dado[2], Dado[3], Dado[4], Dado[5], Dado[6], Dado[7]);
endmodule

module BancoReg (
  input  [3:0] Endereco,
  input  [7:0] Dados_In,
  input  Clock,
  input  WE,
  input  Pino_R,
  output [7:0] Dados_Out
);

  wire and_1_out, and_2_out, and_3_out, and_4_out, and_5_out, and_6_out, and_7_out, and_8_out, and_9_out,
       and_10_out, and_11_out, and_12_out, and_13_out, and_14_out, and_15_out, and_16_out, decoder_1_out0,
       decoder_1_out1, decoder_1_out2, decoder_1_out3, decoder_1_out4, decoder_1_out5, decoder_1_out6,
       decoder_1_out7, decoder_1_out8, decoder_1_out9, decoder_1_out10, decoder_1_out11, decoder_1_out12,
       decoder_1_out13, decoder_1_out14, decoder_1_out15;
  wire [7:0] Reg_0_q, Reg_1_q, Reg_2_q, Reg_3_q, Reg_4_q, Reg_5_q, Reg_6_q, Reg_7_q, Reg_8_q, Reg_9_q,
       Reg_10_q, Reg_11_q, Reg_12_q, Reg_13_q, Reg_14_q, Reg_15_q;

  Decoder #(.enable("false"), .select(4)) decoder_1 (
    .out0(decoder_1_out0), .out1(decoder_1_out1), .out2(decoder_1_out2), .out3(decoder_1_out3),
    .out4(decoder_1_out4), .out5(decoder_1_out5), .out6(decoder_1_out6), .out7(decoder_1_out7),
    .out8(decoder_1_out8), .out9(decoder_1_out9), .out10(decoder_1_out10), .out11(decoder_1_out11),
    .out12(decoder_1_out12), .out13(decoder_1_out13), .out14(decoder_1_out14), .out15(decoder_1_out15),
    .sel(Endereco));
  Register Reg_11 (.D(Dados_In), .en(and_1_out), .clk(Clock), .Q(Reg_11_q), .clr(Pino_R));
  and and_1 (and_1_out, decoder_1_out11, Pino_R);
  and and_2 (and_2_out, decoder_1_out13, Pino_R);
  Register Reg_13 (.D(Dados_In), .en(and_2_out), .clk(Clock), .Q(Reg_13_q), .clr(Pino_R));
  and and_3 (and_3_out, decoder_1_out0, Pino_R);
  Register Reg_0 (.D(Dados_In), .en(and_3_out), .clk(Clock), .Q(Reg_0_q), .clr(Pino_R));
  Register Reg_4 (.D(Dados_In), .en(and_4_out), .clk(Clock), .Q(Reg_4_q), .clr(Pino_R));
  and and_4 (and_4_out, decoder_1_out4, Pino_R);
  Register Reg_7 (.D(Dados_In), .en(and_5_out), .clk(Clock), .Q(Reg_7_q), .clr(Pino_R));
  and and_5 (and_5_out, decoder_1_out7, Pino_R);
  Register Reg_10 (.D(Dados_In), .en(and_6_out), .clk(Clock), .Q(Reg_10_q), .clr(Pino_R));
  and and_6 (and_6_out, decoder_1_out10, Pino_R);
  Register Reg_15 (.D(Dados_In), .en(and_7_out), .clk(Clock), .Q(Reg_15_q), .clr(Pino_R));
  and and_7 (and_7_out, decoder_1_out15, Pino_R);
  and and_8 (and_8_out, decoder_1_out1, Pino_R);
  and and_9 (and_9_out, decoder_1_out3, Pino_R);
  and and_10 (and_10_out, decoder_1_out5, Pino_R);
  and and_11 (and_11_out, decoder_1_out6, Pino_R);
  and and_12 (and_12_out, decoder_1_out8, Pino_R);
  and and_13 (and_13_out, decoder_1_out9, Pino_R);
  and and_14 (and_14_out, decoder_1_out14, Pino_R);
  Register Reg_1 (.D(Dados_In), .en(and_8_out), .clk(Clock), .Q(Reg_1_q), .clr(Pino_R));
  Register Reg_3 (.D(Dados_In), .en(and_9_out), .clk(Clock), .Q(Reg_3_q), .clr(Pino_R));
  Register Reg_5 (.D(Dados_In), .en(and_10_out), .clk(Clock), .Q(Reg_5_q), .clr(Pino_R));
  Register Reg_6 (.D(Dados_In), .en(and_11_out), .clk(Clock), .Q(Reg_6_q), .clr(Pino_R));
  Register Reg_8 (.D(Dados_In), .en(and_12_out), .clk(Clock), .Q(Reg_8_q), .clr(Pino_R));
  Register Reg_9 (.D(Dados_In), .en(and_13_out), .clk(Clock), .Q(Reg_9_q), .clr(Pino_R));
  Register Reg_12 (.D(Dados_In), .en(and_15_out), .clk(Clock), .Q(Reg_12_q), .clr(Pino_R));
  and and_15 (and_15_out, decoder_1_out12, Pino_R);
  Register Reg_14 (.D(Dados_In), .en(and_14_out), .clk(Clock), .Q(Reg_14_q), .clr(Pino_R));
  Register Reg_2 (.D(Dados_In), .en(and_16_out), .clk(Clock), .Q(Reg_2_q));  // open: clr
  and and_16 (and_16_out, decoder_1_out2, Pino_R);
  Multiplexer #(.select(4), .width(8)) multiplexer_1 (
    .in0(Reg_0_q), .in1(Reg_1_q), .in2(Reg_2_q), .in3(Reg_3_q), .in4(Reg_4_q), .in5(Reg_5_q), .in6(Reg_6_q),
    .in7(Reg_7_q), .in8(Reg_8_q), .in9(Reg_9_q), .in10(Reg_10_q), .in11(Reg_11_q), .in12(Reg_12_q),
    .in13(Reg_13_q), .in14(Reg_14_q), .in15(Reg_15_q), .out(Dados_Out), .sel(Endereco));

  assign WE = Pino_R;
endmodule

module Entrada (
  input  in_1,
  input  in_2
);
endmodule
