// Logisim project parte2_cabeada.circ as structural Verilog: 1 circuit, main circuit parte2_cabeada
module parte2_cabeada (
  input  Op_BEQ,
  output PCWrite,
  output MemRead,
  output IRWrite,
  output [1:0] ALUSrcB,
  output RegWrite,
  output ALUSrcA,
  output PCWriteCond,
  output PCSource,
  output [1:0] ALUOp
);

  wire and_1_out, and_2_out, and_3_out, and_4_out, clock_1_out, not_1_out, or_2_out, Q0_qn, Q1_qn, Q2_qn;

  Clock clock_1 (.out(clock_1_out));
  // BCD_to_7_Segment_decoder bcd_to_7_segment_decoder_1: pin names not known; wires that end beside it: {1'b0, ALUOp[0], ALUOp[1], ALUSrcB[1]}
  _7_Segment_Display u_7_segment_display_1 ();  // open: g, f, a, b, e, d, c, dp
  D_Flip_Flop Q2 (.D(and_1_out), .clk(clock_1_out), .Q(ALUOp[0]), .Qn(Q2_qn));  // open: preset, reset
  D_Flip_Flop Q1 (.D(or_2_out), .clk(clock_1_out), .Q(ALUOp[1]), .Qn(Q1_qn));  // open: preset, reset
  D_Flip_Flop Q0 (.D(and_4_out), .clk(clock_1_out), .Q(ALUSrcB[1]), .Qn(Q0_qn));  // open: preset, reset
  not not_1 (not_1_out, Op_BEQ);
  and and_1 (and_1_out, Q1_qn, ALUSrcB[1], Op_BEQ);
  and and_2 (and_2_out, ALUOp[1], Q0_qn);
  and and_3 (and_3_out, Q1_qn, ALUSrcB[1], not_1_out);
  and and_4 (and_4_out, Q2_qn, Q0_qn);
  and and_5 (ALUSrcB[0], Q2_qn, Q1_qn, Q0_qn);
  and and_6 (RegWrite, Q2_qn, ALUSrcB[1]);
  or or_1 (ALUSrcA, ALUOp[0], ALUOp[1]);
  or or_2 (or_2_out, and_2_out, and_3_out);

  assign IRWrite = ALUSrcB[0];
  assign MemRead = ALUSrcB[0];
  assign PCSource = ALUOp[0];
  assign PCWrite = ALUSrcB[0];
  assign PCWriteCond = ALUOp[0];

  // Notes on the sheet:
  //   Q2
  //   'Q2
  //   Q1
  //   'Q1
  //   Q0
  //   'Q0
  //   B
  //   'B
endmodule
