// Logisim project parte2_microprogramada.circ as structural Verilog: 1 circuit, main circuit main
module main (
  input  Op_R,
  input  Op_BEQ,
  output PCWriteCond,
  output PCSource,
  output MemRead,
  output IRWrite,
  output RegWrite,
  output PCWrite,
  output [1:0] ALUSrcB,
  output ALUSrcA,
  output [1:0] ALUOp,
  output [1:0] ULAOp
);

  wire clock_1_out, not_1_out, not_2_out, not_3_out, not_4_out, not_5_out;
  wire [1:0] rom_1_data;
  wire [2:0] adder_1_out, counter_1_q, multiplexer_1_out;
  wire [5:2] rom_1_data_2;

  Clock clock_1 (.out(clock_1_out));
  Counter #(.max('h7), .width(3)) counter_1 (
    .clr(1'b0), .clk(clock_1_out), .D(multiplexer_1_out), .Q(counter_1_q));  // open: load, up, count, carry
  Adder #(.width(3)) adder_1 (.a(counter_1_q), .b(3'b111), .out(adder_1_out));  // open: cin, cout
  ROM #(.addrWidth(3)) rom_1 (.addr(counter_1_q), .data({ALUOp, rom_1_data_2, rom_1_data}));
  Multiplexer #(.select(2), .width(3)) multiplexer_1 (
    .in0(adder_1_out), .in2({Op_BEQ, Op_R, 1'b0}), .out(multiplexer_1_out), .sel(rom_1_data));  // open: in1, in3
  not not_1 (not_1_out, rom_1_data_2[3]);
  not not_2 (not_2_out, rom_1_data_2[4]);
  not not_3 (not_3_out, rom_1_data_2[5]);
  not not_4 (not_4_out, rom_1_data_2[5]);
  and and_1 (IRWrite, rom_1_data_2[2], not_1_out);
  and and_2 (ALUSrcB[0], not_2_out, not_3_out);
  and and_3 (ALUSrcA, rom_1_data_2[4], not_4_out);
  and and_4 (ALUSrcB[1], rom_1_data_2[4], rom_1_data_2[5]);
  and and_5 (PCSource, rom_1_data_2[2], rom_1_data_2[3]);
  not not_5 (not_5_out, rom_1_data_2[2]);
  and and_6 (RegWrite, not_5_out, rom_1_data_2[3]);

  assign MemRead = IRWrite;
  assign PCWrite = ALUSrcB[0];
  assign PCWriteCond = PCSource;
  assign ULAOp = ALUOp;

  // Notes on the sheet:
  //   contents of rom_1 (hex, n*v repeats v):
  //   4 22 90 9 5d
endmodule
